# Fritzing sketch Memory Module (saved by Fritzing 0.9.3b)
breadboards: 1

parts:
  Part1 = Arduino Nano (Rev3.0)
  J1 = Piezo Speaker
  U2 = 7-SEGMENT-DISPLAY-1_-RED [package=7-segment-1_pth]
  S1 = SWITCH-MOMENTARY-2 [package=tactile-pth-12mm]
  S2 = SWITCH-MOMENTARY-2 [package=tactile-pth-12mm]
  S3 = SWITCH-MOMENTARY-2 [package=tactile-pth-12mm]
  S4 = SWITCH-MOMENTARY-2 [package=tactile-pth-12mm]
  SparkFun_7-Segment-Display-Yellow1 = SparkFun 7-Segment Serial Display-Red [part_number=COM-11441]  # not connected
  D1 = LED_BARGRAPH_10 [package=led_bargaph_10]
  Part2 = Shift Register Breakout - 74HC595

nets:
  GND: Part1.GND, J1.pin1, U2.G1, U2.G2, D1.I_C, D1.G_C, D1.E_C, D1.C_C, D1.A_C, Part2.GND
  N1: Part1.D2, Part2.SERIAL_IN
  N2: Part1.D3, J1.pin2
  N3: Part1.D4, Part2.CLOCK
  N4: Part1.D7, U2.G
  N5: Part1.D8, U2.F
  N6: Part1.D9, U2.A
  N7: Part1.D10, U2.C
  N8: Part1.D11/MOSI, U2.D
  N9: Part1.D12/MISO, U2.B
  VIN: Part1.VIN, Part1.5V, S1.1, S2.1, S3.1, S4.1, Part2.VCC
  N10: Part1.A3, S4.2
  N11: Part1.A2, S3.2
  N12: Part1.A1, S2.2
  N13: Part1.A0, S1.2
  N14: Part1.D13/SCK, U2.E
  N15: D1.A_A, Part2.QE

custom parts:
  SparkFun 7-Segment Serial Display-Red: Description: 4-digit 7-segment displays are really neat little devices, it’s a shame that they can be so cumbersome to control. Well we’ve solved that problem by making them a little bit “smarter.” The SparkFun 7-Segment Serial Display combines a classic 4-digit 7-segment display and an ATMega328 microcontroller allowing you to control every segment individually using only a few serial lines.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
