# Fritzing sketch keypad module (saved by Fritzing 0.9.3b)
breadboards: 3

parts:
  Nokia_5110_LCD_Module4 = Nokia 5110 LCD
  Nokia_5110_LCD_Module1 = Nokia 5110 LCD
  Nokia_5110_LCD_Module3 = Nokia 5110 LCD
  Part1 = TXB0108 8-channel Bi-directional Logic Level Converter
  U1 = V_REG_LD1117VXX [package=78xxl]
  Nokia_5110_LCD_Module2 = Nokia 5110 LCD
  R1 = Resistor [tolerance=±5% resistance=330 package=THT]
  R2 = Resistor [tolerance=±5% resistance=330 package=THT]
  R3 = Resistor [tolerance=±5% resistance=330 package=THT]
  R4 = Resistor [tolerance=±5% resistance=330 package=THT]
  Part2 = Arduino Nano (Rev3.0)
  R5 = Resistor [tolerance=±5% resistance=330 package=THT]
  R6 = Resistor [tolerance=±5% resistance=330 package=THT]
  R7 = Resistor [tolerance=±5% resistance=330 package=THT]
  R8 = Resistor [tolerance=±5% resistance=330 package=THT]
  Part7 = LED Tactile Button Breakout v10 [part_number=BOB-10467]  # not connected
  Part8 = LED Tactile Button Breakout v10 [part_number=BOB-10467]  # not connected
  Part9 = LED Tactile Button Breakout v10 [part_number=BOB-10467]  # not connected
  Part10 = LED Tactile Button Breakout v10 [part_number=BOB-10467]  # not connected

nets:
  VCC: Nokia_5110_LCD_Module4.VCC, Nokia_5110_LCD_Module4.VCC_(out), Nokia_5110_LCD_Module1.VCC, Nokia_5110_LCD_Module1.VCC_(out), Nokia_5110_LCD_Module3.VCC, Nokia_5110_LCD_Module3.VCC_(out), Part1.OE, Part1.VCCA, U1.OUT, Nokia_5110_LCD_Module2.VCC, Nokia_5110_LCD_Module2.VCC_(out)
  GND: Nokia_5110_LCD_Module4.GND, Nokia_5110_LCD_Module4.GND_(out), Nokia_5110_LCD_Module1.GND, Nokia_5110_LCD_Module1.GND_(out), Nokia_5110_LCD_Module3.GND, Nokia_5110_LCD_Module3.GND_(out), Part1.GND, U1.GND, Nokia_5110_LCD_Module2.GND, Nokia_5110_LCD_Module2.GND_(out), Part2.GND, R5.Pin_1, R6.Pin_1, R7.Pin_1, R8.Pin_1
  N1: Nokia_5110_LCD_Module4.SCE, Nokia_5110_LCD_Module4.SCE_(out), Part1.A5
  N2: Nokia_5110_LCD_Module4.RST, Nokia_5110_LCD_Module4.RST_(out), Nokia_5110_LCD_Module1.RST, Nokia_5110_LCD_Module1.RST_(out), Nokia_5110_LCD_Module3.RST, Nokia_5110_LCD_Module3.RST_(out), Part1.A4, Nokia_5110_LCD_Module2.RST, Nokia_5110_LCD_Module2.RST_(out)
  N3: Nokia_5110_LCD_Module4.D/C, Nokia_5110_LCD_Module4.D/C_(out), Nokia_5110_LCD_Module1.D/C, Nokia_5110_LCD_Module1.D/C_(out), Nokia_5110_LCD_Module3.D/C, Nokia_5110_LCD_Module3.D/C_(out), Part1.A3, Nokia_5110_LCD_Module2.D/C, Nokia_5110_LCD_Module2.D/C_(out)
  N4: Nokia_5110_LCD_Module4.DN(MOSI), Nokia_5110_LCD_Module4.DN(MODI)_(out), Nokia_5110_LCD_Module1.DN(MOSI), Nokia_5110_LCD_Module1.DN(MODI)_(out), Nokia_5110_LCD_Module3.DN(MOSI), Nokia_5110_LCD_Module3.DN(MODI)_(out), Part1.A2, Nokia_5110_LCD_Module2.DN(MOSI), Nokia_5110_LCD_Module2.DN(MODI)_(out)
  N5: Nokia_5110_LCD_Module4.SCLK, Nokia_5110_LCD_Module4.SCLK_(out), Nokia_5110_LCD_Module1.SCLK, Nokia_5110_LCD_Module1.SCLK_(out), Nokia_5110_LCD_Module3.SCLK, Nokia_5110_LCD_Module3.SCLK_(out), Part1.A1, Nokia_5110_LCD_Module2.SCLK, Nokia_5110_LCD_Module2.SCLK_(out)
  N6: Nokia_5110_LCD_Module4.LED, Nokia_5110_LCD_Module4.LED_(out), R3.Pin_0
  N7: Nokia_5110_LCD_Module1.SCE, Nokia_5110_LCD_Module1.SCE_(out), Part1.A8
  N8: Nokia_5110_LCD_Module1.LED, Nokia_5110_LCD_Module1.LED_(out), R1.Pin_0
  N9: Nokia_5110_LCD_Module3.SCE, Nokia_5110_LCD_Module3.SCE_(out), Part1.A6
  N10: Nokia_5110_LCD_Module3.LED, Nokia_5110_LCD_Module3.LED_(out), R4.Pin_0
  N11: Part1.VCCB, U1.IN, R1.Pin_1, R2.Pin_1, R3.Pin_1, R4.Pin_1, Part2.VIN
  N12: Part1.B1, Part2.D13/SCK
  N13: Part1.B2, Part2.D11/MOSI
  N14: Part1.B3, Part2.D5
  N15: Part1.B4, Part2.D6
  N16: Part1.B5, Part2.D7
  N17: Part1.B6, Part2.D8
  N18: Part1.B7, Part2.D9
  N19: Part1.B8, Part2.D10
  N20: Part1.A7, Nokia_5110_LCD_Module2.SCE, Nokia_5110_LCD_Module2.SCE_(out)
  N21: Nokia_5110_LCD_Module2.LED, Nokia_5110_LCD_Module2.LED_(out), R2.Pin_0

custom parts:
  Nokia 5110 LCD: Nokia 5110 Graphic 84*48 LCD module such as the Sparkfun LCD-10168 or the clones from Ebay. There is example code for the Arduino available from the Sparkfun site in https://learn.sparkfun.com/tutorials/graphic-lcd-hookup-guide This is a 3.3V device, if you are running it from a 5V micro you need a 5V tolorant level translator such as the 74ahc367 to protect the signal imputs. Rafa G. did a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
  TXB0108 8-channel Bi-directional Logic Level Converter: Because the Arduino (and Basic Stamp) are 5V devices, and most modern sensors, displays, flash cards and modes are 3.3V-only, many makers find that they need to perform level shifting/conversion to protect the 3.3V device from 5V. Although one can use resistors to make a divider, for high speed transfers, the resistors can add a lot of slew and cause havoc that is tough to debug. For that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
  LED Tactile Button Breakout v10: This simple breakout board makes it easy to use our LED tactile switches in a breadboard, or your next project.
