# Fritzing sketch timerModule (saved by Fritzing 0.9.3b)
circuit board: 5.64444cm x 8.46667cm
breadboards: 1

parts:
  Part1 = Arduino Nano (Rev3.0)
  LED1 = LED - 5mm [color="Red (633nm)" package="5 mm [THT]"]
  LED2 = LED - 5mm [color="Red (633nm)" package="5 mm [THT]"]
  LED3 = LED - 5mm [color="Red (633nm)" package="5 mm [THT]"]
  R1 = Resistor [tolerance=±5% resistance=220 package=THT]
  R2 = Resistor [tolerance=±5% resistance=220 package=THT]
  R3 = Resistor [tolerance=±5% resistance=220 package=THT]
  R5 = Resistor [tolerance=±5% resistance=10k package=THT]
  R6 = Resistor [tolerance=±5% resistance=10k package=THT]
  J1 = Piezo Speaker
  R7 = Resistor [tolerance=±5% resistance=100 package=THT]
  S1 = Pushbutton [package="[THT]"]
  R8 = Resistor [tolerance=±5% resistance=10k package=THT]
  S2 = Pushbutton [package="[THT]"]
  R9 = Resistor [tolerance=±5% resistance=10k package=THT]
  PART1 = OpenSegment Serial Display - 20mm (Blue) [part_number=COM-11647]

nets:
  GND: Part1.GND, R1.Pin_0, R2.Pin_0, R3.Pin_0, J1.pin1, R8.Pin_1, R9.Pin_1, PART1.GND, PART1.-
  N1: Part1.D2, PART1.RX
  N2: Part1.D3, R7.Pin_0
  N3: Part1.D4, S1.Pin_1, S1.Pin_2, R8.Pin_0
  N4: Part1.D5, S2.Pin_1, S2.Pin_2, R9.Pin_0
  N5: Part1.D7, LED3.anode
  N6: Part1.D8, LED2.anode
  N7: Part1.D9, LED1.anode
  VIN: Part1.VIN, R5.Pin_0, R6.Pin_0, S1.Pin_3, S1.Pin_4, S2.Pin_3, S2.Pin_4, PART1.VCC, PART1.+
  N8: Part1.A5, R6.Pin_1
  N9: Part1.A4, R5.Pin_1
  N10: LED1.cathode, R1.Pin_1
  N11: LED2.cathode, R2.Pin_1
  N12: LED3.cathode, R3.Pin_1
  N13: J1.pin2, R7.Pin_1

custom parts:
  OpenSegment Serial Display - 20mm (Blue): OpenSegment makes it easy to add a large 7-segment display to your project. Because larger 7-segment displays pull more power than a microcontroller is able to drive directly, the OpenSegment has 8 PNP and 4 NPN transistors in order to drive the segments at their maximum brightness! The on-board ATmega328 receives data over multiple digital interfaces (such as TWI, UART and SPI) and does all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
